# Fritzing sketch 328_term (saved by Fritzing 0.9.1b)
breadboards: 1

parts:
  JP1 = RCA [package=rca_lock]
  U1 = mini DIN 6 Connector [package=mini-din6]  # not connected
  U2 = atmega328 [package=dip]  # not connected
  U3 = atmega328 [package=dip]
  D1_1N4148 = Diode [package=diode-1n4148]
  D2_1N4148 = Diode [package=diode-1n4148]
  R1 = Resistor [tolerance=±5% resistance=1k package="1206 [SMD]"]
  R2 = Resistor [tolerance=±5% resistance=330 package="1206 [SMD]"]
  XTAL1 = Crystal [frequency="16 Mhz" package=THT]
  C1_-_22pf = Capacitor [package=cap-pth-small2]
  C2_-_22pf = Capacitor [package=cap-pth-small2]

nets:
  N1: JP1.PIN, R1.Pin_1, R2.Pin_1
  GND: JP1.SHELL, C1_-_22pf.2, C2_-_22pf.2
  N2: U3.XLAT1, XTAL1.pin_1, C2_-_22pf.1
  N3: U3.XLAT2, XTAL1.pin_0, C1_-_22pf.1
  N4: U3.D9_(PWM), D1_1N4148.A
  N5: U3.D11_(PWM), D2_1N4148.A
  N6: D1_1N4148.C, R1.Pin_0
  N7: D2_1N4148.C, R2.Pin_0

notes:
  sig_pixel
  sig_sync
